# Fritzing sketch R.Ian_perfboard (saved by Fritzing 0.9.2b)
perfboards: 1

parts:
  Composant1 = Arduino Nano (Rev3.0)
  S1 = Toggle Switch [package=THT]
  U1 = Voltage Regulator - 5V [package="TO220 [THT]"]
  VCC1 = Battery
  S2 = Pushbutton [package="[THT]"]
  S3 = Pushbutton [package="[THT]"]
  J2 = Infrared Proximity Sensor

nets:
  GND: Composant1.GND, U1.GND, S2.Pin_1, S2.Pin_2, S3.Pin_1, S3.Pin_2, J2.GND
  N1: Composant1.D4, S3.Pin_3, S3.Pin_4
  N2: Composant1.D5, S2.Pin_3, S2.Pin_4
  5V: Composant1.5V, U1.output_voltage, J2.Vcc
  N3: Composant1.A0, J2.Vout
  N4: S1.L1, VCC1.+
  N5: S1.COM, U1.input_voltage

notes:
  sensorServo
  leftServo
  rightServo
  leftContactSwith
  rightContactSwith
